# Fritzing sketch Witty_DH22 (saved by Fritzing 0.9.3b)
breadboards: 1

parts:
  RHT1 = Humidity and Temperature Sensor RHT03
  WiFi-Witty-Gizwits-ESP-12F1 = WiFi-Witty-Gizwits-ESP-12F
  hc-sr1 = hc-sr04
  Squix1 = OLED 0.96" 128x64 I2C SSD1306

nets:
  VCC: RHT1.Vcc, WiFi-Witty-Gizwits-ESP-12F1.VCC, hc-sr1.VCC, Squix1.VCC
  N1: RHT1.Data-signal, WiFi-Witty-Gizwits-ESP-12F1.GPIO14
  GND: RHT1.GND_2, WiFi-Witty-Gizwits-ESP-12F1.GND, hc-sr1.GND, Squix1.GND
  N2: WiFi-Witty-Gizwits-ESP-12F1.GPIO12, hc-sr1.Trig
  N3: WiFi-Witty-Gizwits-ESP-12F1.GPIO13, hc-sr1.Echo
  N4: WiFi-Witty-Gizwits-ESP-12F1.GPIO4, Squix1.SCA
  N5: WiFi-Witty-Gizwits-ESP-12F1.GPIO5, Squix1.SCL

custom parts:
  WiFi-Witty-Gizwits-ESP-12F: A breadboard friendly two part WiFi development board by Gizwits, powered by an ESP8266 ESP-12F SoC, featuring twin micro-usb ports, a photoresistor, a WS2812 RGB-LED and three buttons. The board comes in two parts. The bottom half has reset and flash buttons, a micro-usb with CH340 UART and 2x 1x08 female headers. The top half has the ESP-12F, LDR, RGB-LED, micro-usb (for power only), an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
